# Fritzing sketch Receiver_new (saved by Fritzing 0.8.7b)
breadboards: 1

parts:
  Arduino_Nano = Arduino Nano (Rev3.0)
  Transceiver2 = nRF24L01 [package=module]
  LED2 = LED - 5mm [color="Red (633nm)" package="5 mm [THT]"]
  1Ch_Relay_Module = Jtron 1 Channel Optoisolated Relay Module [package=relay]
  Speaker = SPEAKER [package=pcb_mount_speaker]
  12V_Power_supply = Battery block 9V

nets:
  GND: Arduino_Nano.GND, Transceiver2.GND, LED2.anode, 1Ch_Relay_Module.GND, Speaker.+, 12V_Power_supply.-
  N1: Arduino_Nano.D4, 1Ch_Relay_Module.IN1
  N2: Arduino_Nano.D5, LED2.cathode
  N3: Arduino_Nano.D6, Transceiver2.CE
  N4: Arduino_Nano.D7, Transceiver2.CSN
  N5: Arduino_Nano.D10, Arduino_Nano.D11/MOSI, Transceiver2.MOSI
  N6: Arduino_Nano.D12/MISO, Transceiver2.MISO
  N7: Arduino_Nano.VIN, 12V_Power_supply.+
  VCC: Arduino_Nano.5V, Transceiver2.VCC, 1Ch_Relay_Module.VCC
  N8: Arduino_Nano.3V3, Arduino_Nano.D13/SCK, Transceiver2.SCK
  N9: 1Ch_Relay_Module.NO, Speaker.-

custom parts:
  nRF24L01: nRF24L01 module
