# Fritzing sketch Transmitter_new (saved by Fritzing 0.8.7b)
breadboards: 1

parts:
  Part2 = Arduino Nano (Rev3.0)
  Transceiver2 = nRF24L01 [package=module]
  LED2 = LED - 5mm [color="Red (633nm)" package="5 mm [THT]"]
  VCC1 = Battery block 9V

nets:
  GND: Part2.GND, Transceiver2.GND, LED2.anode, VCC1.-
  N1: Part2.D3, LED2.cathode
  N2: Part2.D7, Transceiver2.CE
  N3: Part2.D8, Transceiver2.CSN
  N4: Part2.D11/MOSI, Transceiver2.MOSI
  N5: Part2.D12/MISO, Transceiver2.MISO
  N6: Part2.VIN, VCC1.+
  5V: Part2.5V, Transceiver2.VCC
  N7: Part2.D13/SCK, Transceiver2.SCK

custom parts:
  nRF24L01: nRF24L01 module
